# Fritzing sketch 3MiniPro1PCB (saved by Fritzing 0.9.0b)
perfboards: 1

parts:
  Part1 = Arduino Pro Mini v13
  Part2 = Arduino Pro Mini v13
  Part3 = Arduino Pro Mini v13
  R17 = Resistor [tolerance=±5% resistance=220 package="0603 [SMD]"]
  R18 = Resistor [tolerance=±5% resistance=220 package="0603 [SMD]"]
  R19 = Resistor [tolerance=±5% resistance=220 package="0603 [SMD]"]
  R20 = Resistor [tolerance=±5% resistance=220 package="0603 [SMD]"]
  R21 = Resistor [tolerance=±5% resistance=220 package="0603 [SMD]"]
  R22 = Resistor [tolerance=±5% resistance=220 package="0603 [SMD]"]
  R23 = Resistor [tolerance=±5% resistance=220 package="0603 [SMD]"]
  R24 = Resistor [tolerance=±5% resistance=220 package="0603 [SMD]"]
  R25 = Resistor [tolerance=±5% resistance=220 package="0603 [SMD]"]
  R26 = Resistor [tolerance=±5% resistance=220 package="0603 [SMD]"]
  R27 = Resistor [tolerance=±5% resistance=220 package="0603 [SMD]"]
  R28 = Resistor [tolerance=±5% resistance=220 package="0603 [SMD]"]
  R29 = Resistor [tolerance=±5% resistance=220 package="0603 [SMD]"]
  R30 = Resistor [tolerance=±5% resistance=220 package="0603 [SMD]"]
  R31 = Resistor [tolerance=±5% resistance=220 package="0603 [SMD]"]
  R32 = Resistor [tolerance=±5% resistance=220 package="0603 [SMD]"]
  R33 = Resistor [tolerance=±5% resistance=220 package="0603 [SMD]"]
  R34 = Resistor [tolerance=±5% resistance=220 package="0603 [SMD]"]  # not connected
  J1 = male pin header, 4 pins [form="♂ (male)"]
  J2 = male pin header, 4 pins [form="♂ (male)"]
  J3 = male pin header, 11 pins [form="♂ (male)"]
  J4 = male pin header, 11 pins [form="♂ (male)"]  # not connected
  J5 = male pin header, 11 pins [form="♂ (male)"]  # not connected
  J6 = male pin header, 11 pins [form="♂ (male)"]  # not connected
  J7 = male pin header, 11 pins [form="♂ (male)"]  # not connected
  J8 = male pin header, 11 pins [form="♂ (male)"]  # not connected
  J10 = male pin header, 11 pins [form="♂ (male)"]  # not connected
  J9 = male pin header, 9 pins [form="♂ (male)"]
  J11 = male pin header, 9 pins [form="♂ (male)"]

nets:
  N1: Part1.RAW, J11.pin7
  N2: Part1.GND, R20.Pin_1, R30.Pin_1
  N3: Part1.VCC, R25.Pin_0
  N4: Part2.RAW, Part3.RAW, J9.pin7
  GND: Part2.GND, Part3.GND
  N5: R17.Pin_1, J3.pin4
  N6: R18.Pin_1, R28.Pin_0, J3.pin8
  N7: R19.Pin_0, R33.Pin_0
  N8: R19.Pin_1, J3.pin1
  N9: R20.Pin_0, R23.Pin_1, J3.pin7
  N10: R21.Pin_1, R30.Pin_0, J3.pin11
  N11: R22.Pin_0, R29.Pin_1, J3.pin9
  N12: R24.Pin_1, J3.pin5
  N13: R25.Pin_1, J3.pin3
  N14: R26.Pin_1, J3.pin6
  N15: R27.Pin_0, R31.Pin_1, J3.pin10
  N16: R32.Pin_1, J3.pin2
  N17: J1.pin1, J1.pin4
  N18: J2.pin1, J2.pin4
  N19: J9.pin9, J11.pin9

notes:
  M(2+3)
  S(1+6)
  S(4+5)
