# Fritzing sketch MEGA_ENC_MS (saved by Fritzing 0.9.0b)

parts:
  Part1 = Arduino Mega ADK (Rev3)
  R33 = Resistor [tolerance=±5% resistance=39 package="0603 [SMD]"]  # not connected
  R34 = Resistor [tolerance=±5% resistance=47k package="0603 [SMD]"]  # not connected
  R36 = Resistor [tolerance=±1% resistance=47k package="0603 [SMD]"]  # not connected
  R37 = Resistor [tolerance=±5% resistance=330k package="0603 [SMD]"]  # not connected
  R38 = Resistor [tolerance=±5% resistance=330k package="0603 [SMD]"]  # not connected
  R39 = Resistor [tolerance=±5% resistance=39 package="0603 [SMD]"]  # not connected
  R40 = Resistor [tolerance=±5% resistance=39 package="0603 [SMD]"]  # not connected
  R41 = Resistor [tolerance=±5% resistance=39 package="0603 [SMD]"]  # not connected
  R42 = Resistor [tolerance=±5% resistance=47k package="0603 [SMD]"]  # not connected
  R43 = Resistor [tolerance=±5% resistance=330k package="0603 [SMD]"]  # not connected
  R44 = Resistor [tolerance=±5% resistance=47k package="0603 [SMD]"]
  R45 = Resistor [tolerance=±5% resistance=330k package="0603 [SMD]"]
  R46 = Resistor [tolerance=±5% resistance=39 package="0603 [SMD]"]
  R47 = Resistor [tolerance=±5% resistance=47k package="0603 [SMD]"]  # not connected
  R48 = Resistor [tolerance=±5% resistance=39 package="0603 [SMD]"]  # not connected
  J5 = male pin header, 6 pins [form="♂ (male)"]
  LED1 = Gus the Green LED
  LED2 = Gus the Green LED
  LED3 = Gus the Green LED
  LED4 = Gus the Green LED
  LED5 = Gus the Green LED
  LED6 = Gus the Green LED
  J4 = male pin header, 9 pins [form="♂ (male)"]
  R35 = Resistor [tolerance=±5% resistance=330k package="0603 [SMD]"]  # not connected

nets:
  N1: Part1.D21/SCL, J4.pin1
  N2: Part1.D20/SDA, J4.pin3
  N3: Part1.D19/RX1, J4.pin5
  N4: Part1.GND, R45.Pin_1, LED1.anode, LED2.anode, LED3.anode, LED4.anode, LED5.anode, LED6.anode
  N5: Part1.D2_PWM, J4.pin7
  N6: Part1.D3_PWM, J4.pin9
  N7: R44.Pin_0, R46.Pin_0
  N8: J5.pin1, LED1.cathode
  N9: J5.pin2, LED2.cathode
  N10: J5.pin3, LED3.cathode
  N11: J5.pin4, LED4.cathode
  N12: J5.pin5, LED5.cathode
  N13: J5.pin6, LED6.cathode

notes:
  From MS
  From P1
  From P0
  To LED
