# Fritzing sketch MEGA_oneDriver (saved by Fritzing 0.9.0b)

parts:
  IC1 = L293D [package=THT]
  Part1 = Arduino Mega ADK (Rev3)
  JACK1 = 2.1mm Barrel Jack with Terminal Block
  C1 = Electrolytic Capacitor [capacitance=100μF package="0807 [SMD, electrolytic]"]
  M1 = DC Motor
  M2 = DC Motor

nets:
  N1: IC1.Enable_1, IC1.Enable_2, IC1.+V, Part1.5V
  N2: IC1.In_1, Part1.D37
  N3: IC1.Out_1_(_Controlled_by_Enable_1_), M1.pin_2
  N4: IC1.0V, Part1.GND, JACK1.NEG, C1.-
  N5: IC1.Out_2_(_Controlled_by_Enable_1_), M1.pin_1
  N6: IC1.In_2, Part1.D35
  N7: IC1.+Vmotor, JACK1.POS, C1.+
  N8: IC1.In_3, Part1.D39
  N9: IC1.Out_3_(_Controlled_by_Enable_2_), M2.pin_2
  N10: IC1.Out_4_(_Controlled_by_Enable_2_), M2.pin_1
  N11: IC1.In_4, Part1.D41

notes:
  To 12V
